// Logisim project DataPath.circ as structural Verilog: 17 circuits, main circuit main
module main (
  input  in_1
);

  wire and_1_out, C_ALUSrc, C_BrEq, C_BrNe, C_Jal, C_Jr, C_Jump, C_MemRead, C_MemToReg, C_MemWrite, C_RegDst,
       C_RegWrite, CLK, eq_rt, eq_zero, EX_BranchTaken, EX_Zero, EXMEM_BranchTaken, EXMEM_MemRead,
       EXMEM_MemToReg, EXMEM_MemWrite, EXMEM_RegWrite, IDEX_ALUSrc, IDEX_BrEq, IDEX_BrNe, IDEX_MemRead,
       IDEX_MemToReg, IDEX_MemWrite, IDEX_RegDst, IDEX_RegWrite, IDEXFlush, IFIDFlush, IFIDWrite, JumpOrJal,
       MEMWB_Jal, MEMWB_MemToReg, MEMWB_RegWrite, not_zero, PCWrite, StoreFwdSel, WB_RegWrite;
  wire [1:0] FwdA, FwdB;
  wire [2:0] C_ALUCtrl, EX_WriteReg, EXMEM_Rt, EXMEM_WriteReg, ID_rd, ID_rs, ID_rt, ID_shamt, IDEX_ALUCtrl,
       IDEX_rd, IDEX_rs, IDEX_rt, IDEX_shamt, MEMWB_WriteReg, WB_WriteReg;
  wire [3:0] ID_opcode;
  wire [5:0] ID_imm6;
  wire [11:0] ID_target;
  wire [15:0] cyclecounter_1_count, EX_ALUResult, EX_BranchTarget, EX_rd2, EXMEM_ALUResult,
       EXMEM_BranchTarget, EXMEM_rd2, ID_imm, IDEX_imm, IDEX_pc1, IDEX_rd1, IDEX_rd2, IFID_instr, IFID_pc1,
       IMEM_instr, JumpTarget16, MEM_ReadData, MEMWB_ALUResult, MEMWB_PC1, MEMWB_ReadData, NextPC, PC1_IF,
       PC_after_branch, PC_after_jump, pc_out, RF_rd1, RF_rd2, StoreData_ToMem, WB_WriteData;

  Clock clock_1 (.out(CLK));
  Multiplexer #(.width(16)) multiplexer_1 (
    .in0(PC1_IF), .in1(EX_BranchTarget), .out(PC_after_branch), .sel(EX_BranchTaken));
  CycleCounter cyclecounter_1 (.clk(CLK), .reset(in_1), .count(cyclecounter_1_count));
  // Probe on cyclecounter_1_count
  PC pc_1 (.clk(CLK), .PCWrite(PCWrite), .NextPC(NextPC), .reset(in_1), .PC_plus1(PC1_IF), .PC_Out(pc_out));
  InstructionMemory instructionmemory_1 (.addr16(pc_out), .instr(IMEM_instr));
  IF_ID if_id_1 (
    .instr_in(IMEM_instr), .pc1_in(PC1_IF), .clk(CLK), .IFID_Write(IFIDWrite), .reset(in_1),
    .IFID_Flush(IFIDFlush), .instr_out(IFID_instr), .pc1_out(IFID_pc1));
  or or_1 (JumpOrJal, C_Jump, C_Jal);
  HazardUnit hazardunit_1 (
    .IDEX_rt(IDEX_rt), .IFID_rs(ID_rs), .IFID_rt(ID_rt), .Jump(C_Jump), .Jal(C_Jal), .Jr(C_Jr),
    .BranchTaken(EX_BranchTaken), .IDEX_MemRead(IDEX_MemRead), .PCWrite(PCWrite), .IFID_Write(IFIDWrite),
    .IFID_Flush(IFIDFlush), .IDEX_Flush(IDEXFlush));
  ExtractEnd extractend_1 (
    .instr(IFID_instr), .pc1(IFID_pc1), .opcode(ID_opcode), .rs(ID_rs), .rt(ID_rt), .rd(ID_rd),
    .shamt(ID_shamt), .imm6(ID_imm6), .target12(ID_target), .imm_ext(ID_imm), .jump_target(JumpTarget16));
  Multiplexer #(.width(16)) multiplexer_2 (
    .in0(PC_after_branch), .in1(JumpTarget16), .out(PC_after_jump), .sel(JumpOrJal));
  Multiplexer #(.width(16)) multiplexer_3 (.in0(PC_after_jump), .in1(RF_rd1), .out(NextPC), .sel(C_Jr));
  ControlUnit controlunit_1 (
    .Opcode(ID_opcode), .ALUCtrl(C_ALUCtrl), .RegWrite(C_RegWrite), .MemRead(C_MemRead),
    .MemWrite(C_MemWrite), .MemToReg(C_MemToReg), .RegDst(C_RegDst), .ALUSrc(C_ALUSrc), .BranchEq(C_BrEq),
    .BranchNe(C_BrNe), .Jump(C_Jump), .Jal(C_Jal), .Jr(C_Jr));
  RegisterFile registerfile_1 (
    .wa(WB_WriteReg), .clk(CLK), .wd(WB_WriteData), .reset(in_1), .we(WB_RegWrite), .rs(ID_rs), .rt(ID_rt),
    .rd1(RF_rd1), .rd2(RF_rd2));
  ID_EX id_ex_1 (
    .BranchNe_in(C_BrNe), .ALUCtrl_in(C_ALUCtrl), .MemRead_in(C_MemRead), .MemWrite_in(C_MemWrite),
    .MemToReg_in(C_MemToReg), .RegDst_in(C_RegDst), .ALUSrc_in(C_ALUSrc), .BranchEq_in(C_BrEq),
    .RegWrite_in(C_RegWrite), .IDEX_Flush(IDEXFlush), .pc1_in(IFID_pc1), .rd1_in(RF_rd1), .rd2_in(RF_rd2),
    .imm_in(ID_imm), .rs_in(ID_rs), .rt_in(ID_rt), .rd_in(ID_rd), .shamt_in(ID_shamt), .clk(CLK),
    .reset(in_1), .MemRead_out(IDEX_MemRead), .pc1_out(IDEX_pc1), .rd1_out(IDEX_rd1), .rd2_out(IDEX_rd2),
    .imm_out(IDEX_imm), .rs_out(IDEX_rs), .rt_out(IDEX_rt), .rd_out(IDEX_rd), .shamt_out(IDEX_shamt),
    .RegWrite_out(IDEX_RegWrite), .MemWrite_out(IDEX_MemWrite), .MemToReg_out(IDEX_MemToReg),
    .RegDst_out(IDEX_RegDst), .ALUSrc_out(IDEX_ALUSrc), .BranchEq_out(IDEX_BrEq), .BranchNe_outv(IDEX_BrNe),
    .ALUCtrl_out(IDEX_ALUCtrl));
  EX_Stage ex_stage_1 (
    .BranchEq(IDEX_BrEq), .BranchNe(IDEX_BrNe), .rd1(IDEX_rd1), .EXMEM_ALUResult(EXMEM_ALUResult),
    .MEMWB_WriteData(WB_WriteData), .rd2(IDEX_rd2), .imm(IDEX_imm), .ForwardA(FwdA), .ForwardB(FwdB),
    .rt(IDEX_rt), .rd(IDEX_rd), .ALUSrc(IDEX_ALUSrc), .RegDst(IDEX_RegDst), .shamt(IDEX_shamt),
    .ALUCtrl(IDEX_ALUCtrl), .pc1(IDEX_pc1), .WriteReg(EX_WriteReg), .BranchTarget(EX_BranchTarget),
    .ALUResult(EX_ALUResult), .BranchTaken(EX_BranchTaken), .Zero(EX_Zero), .B_fwd(EX_rd2));
  ForwardingUnit forwardingunit_1 (
    .EXMEM_Rd(EXMEM_WriteReg), .MEMWB_Rd(MEMWB_WriteReg), .IDEX_rt(IDEX_rt), .IDEX_rs(IDEX_rs),
    .MEMWB_RegWrite(MEMWB_RegWrite), .EXMEM_RegWrite(EXMEM_RegWrite), .ForwardA(FwdA), .ForwardB(FwdB));
  EX_MEM ex_mem_1 (
    .Rt_in(IDEX_rt), .MemToReg_in(IDEX_MemToReg), .RegWrite_in(IDEX_RegWrite), .ALUResult_in(EX_ALUResult),
    .rd2_in(EX_rd2), .WriteReg_in(EX_WriteReg), .BranchTarget_in(EX_BranchTarget),
    .BranchTaken_in(EX_BranchTaken), .MemRead_in(IDEX_MemRead), .MemWrite_in(IDEX_MemWrite), .clk(CLK),
    .reset(in_1), .ALUResult_out(EXMEM_ALUResult), .rd2_out(EXMEM_rd2), .WriteReg_out(EXMEM_WriteReg),
    .BranchTarget_out(EXMEM_BranchTarget), .BranchTaken_out(EXMEM_BranchTaken), .MemRead_out(EXMEM_MemRead),
    .MemToReg_out(EXMEM_MemToReg), .RegWrite_out(EXMEM_RegWrite), .Rt_out(EXMEM_Rt),
    .MemWrite_out(EXMEM_MemWrite));
  and and_1 (and_1_out, MEMWB_RegWrite, eq_rt);
  Comparator #(.width(3)) comparator_1 (.a(MEMWB_WriteReg), .b(EXMEM_Rt), .eq(eq_rt));  // open: gt, lt
  Comparator #(.width(3)) comparator_2 (.a(MEMWB_WriteReg), .b(3'b000), .eq(eq_zero));  // open: gt, lt
  not not_1 (not_zero, eq_zero);
  DataMemory datamemory_1 (
    .Addr(EXMEM_ALUResult), .WriteData(EXMEM_rd2), .MemRead(EXMEM_MemRead), .MemWrite(EXMEM_MemWrite),
    .clk(CLK), .ReadData(MEM_ReadData));
  and and_2 (StoreFwdSel, and_1_out, not_zero);
  MEM_WB mem_wb_1 (
    .ALUResult_in(EXMEM_ALUResult), .WriteReg_in(EXMEM_WriteReg), .PC1_in(IDEX_pc1),
    .RegWrite_in(EXMEM_RegWrite), .ReadData_in(MEM_ReadData), .MemToReg_in(EXMEM_MemToReg), .Jal_in(C_Jal),
    .clk(CLK), .reset(in_1), .WriteReg_out(MEMWB_WriteReg), .ALUResult_out(MEMWB_ALUResult),
    .ReadData_out(MEMWB_ReadData), .PC1_out(MEMWB_PC1), .MemToReg_out(MEMWB_MemToReg), .Jal_out(MEMWB_Jal),
    .RegWrite_out(MEMWB_RegWrite));
  Multiplexer #(.width(16)) multiplexer_4 (
    .in0(EXMEM_rd2), .in1(WB_WriteData), .out(StoreData_ToMem), .sel(StoreFwdSel));
  WBStage wbstage_1 (
    .ReadData(MEMWB_ReadData), .ALUResult(MEMWB_ALUResult), .PC1(MEMWB_PC1), .MemToReg(MEMWB_MemToReg),
    .WriteReg_in(MEMWB_WriteReg), .Jal(MEMWB_Jal), .RegWrite_in(MEMWB_RegWrite), .WriteReg_out(WB_WriteReg),
    .RegWrite_out(WB_RegWrite), .WriteData_out(WB_WriteData));

  // Other names for the same wires on the sheet: RST = in_1

  // Notes on the sheet:
  //   Cycle counter
endmodule

module PC (
  input  clk,
  input  PCWrite,
  input  [15:0] NextPC,
  input  reset,
  output [15:0] PC_plus1,
  output [15:0] PC_Out
);

  Register #(.width(16)) register_1 (.D(NextPC), .en(PCWrite), .clk(clk), .Q(PC_Out), .clr(reset));
  // Probe on PC_Out
  Adder #(.width(16)) adder_1 (.a(PC_Out), .b(16'h1), .out(PC_plus1), .cin(1'b0));  // open: cout
endmodule

module InstructionMemory (
  input  [15:0] addr16,
  output [15:0] instr
);

  ROM #(.dataWidth(16)) rom_1 (.addr(addr16[7:0]), .data(instr));

  // Notes on the sheet:
  //   contents of rom_1 (hex, n*v repeats v):
  //   9041 90c0 9108 9140 a706 1a40 9b42 2250 2448 96c1 c004 2000
endmodule

module IF_ID (
  input  [15:0] instr_in,
  input  IFID_Flush,
  input  clk,
  input  IFID_Write,
  input  reset,
  input  [15:0] pc1_in,
  output [15:0] instr_out,
  output [15:0] pc1_out
);

  wire [15:0] multiplexer_1_out;

  Multiplexer #(.width(16)) multiplexer_1 (.in0(instr_in), .in1({16{1'b0}}), .out(multiplexer_1_out), .sel(IFID_Flush));
  Register #(.width(16)) register_1 (.D(multiplexer_1_out), .en(IFID_Write), .clk(clk), .Q(instr_out), .clr(reset));
  Register #(.width(16)) register_2 (.D(pc1_in), .en(IFID_Write), .clk(clk), .Q(pc1_out), .clr(reset));
endmodule

module ExtractEnd (
  input  [15:0] instr,
  input  [15:0] pc1,
  output [3:0] opcode,
  output [2:0] rs,
  output [2:0] rt,
  output [2:0] rd,
  output [2:0] shamt,
  output [5:0] imm6,
  output [11:0] target12,
  output [15:0] imm_ext,
  output [15:0] jump_target
);

  assign imm_ext = {{10{instr[5]}}, instr[5:0]};  // Bit_Extender bit_extender_1

  assign imm6 = instr[5:0];
  assign jump_target = {pc1[15:12], instr[11:0]};
  assign opcode = instr[15:12];
  assign rd = instr[5:3];
  assign rs = instr[11:9];
  assign rt = instr[8:6];
  assign shamt = instr[2:0];
  assign target12 = instr[11:0];

  // Notes on the sheet:
  //   pc1_hi4
endmodule

module RegisterFile (
  input  clk,
  input  [15:0] wd,
  input  [2:0] rs,
  input  we,
  input  [2:0] wa,
  input  reset,
  input  [2:0] rt,
  output [15:0] rd1,
  output [15:0] rd2
);

  wire and_1_out, and_2_out, decoder_1_out1, decoder_1_out2, decoder_1_out3, decoder_1_out4, decoder_1_out5,
       decoder_1_out6, decoder_1_out7, eq0, eq1, eq2, hit1, hit2, waNotZero;
  wire [15:0] multiplexer_1_out, multiplexer_2_out, r0_q, r1_q, r2_q, r3_q, r4_q, r5_q, r6_q, r7_q;

  Decoder #(.select(3)) decoder_1 (
    .out1(decoder_1_out1), .out2(decoder_1_out2), .out3(decoder_1_out3), .out4(decoder_1_out4),
    .out5(decoder_1_out5), .out6(decoder_1_out6), .out7(decoder_1_out7), .sel(wa), .en(we));  // open: out0
  Comparator #(.width(3)) comparator_1 (.a(wa), .b(rs), .eq(eq1));  // open: gt, lt
  Comparator #(.width(3)) comparator_2 (.a(wa), .b(rt), .eq(eq2));  // open: gt, lt
  Comparator #(.width(3)) comparator_3 (.a(wa), .b(3'b000), .eq(eq0));  // open: gt, lt
  Register #(.width(16)) r0 (.D(wd), .en(1'b0), .clk(clk), .Q(r0_q), .clr(reset));
  Register #(.width(16)) r1 (.D(wd), .en(decoder_1_out1), .clk(clk), .Q(r1_q), .clr(reset));
  Register #(.width(16)) r2 (.D(wd), .en(decoder_1_out2), .clk(clk), .Q(r2_q), .clr(reset));
  Register #(.width(16)) r3 (.D(wd), .en(decoder_1_out3), .clk(clk), .Q(r3_q), .clr(reset));
  Register #(.width(16)) r4 (.D(wd), .en(decoder_1_out4), .clk(clk), .Q(r4_q), .clr(reset));
  Register #(.width(16)) r5 (.D(wd), .en(decoder_1_out5), .clk(clk), .Q(r5_q), .clr(reset));
  Register #(.width(16)) r6 (.D(wd), .en(decoder_1_out6), .clk(clk), .Q(r6_q), .clr(reset));
  Register #(.width(16)) r7 (.D(wd), .en(decoder_1_out7), .clk(clk), .Q(r7_q), .clr(reset));
  not not_1 (waNotZero, eq0);
  and and_1 (and_1_out, we, waNotZero);
  and and_2 (and_2_out, we, waNotZero);
  Multiplexer #(.select(3), .width(16)) multiplexer_1 (
    .in0(r0_q), .in1(r1_q), .in2(r2_q), .in3(r3_q), .in4(r4_q), .in5(r5_q), .in6(r6_q), .in7(r7_q),
    .out(multiplexer_1_out), .sel(rs));
  Multiplexer #(.select(3), .width(16)) multiplexer_2 (
    .in0(r0_q), .in1(r1_q), .in2(r2_q), .in3(r3_q), .in4(r4_q), .in5(r5_q), .in6(r6_q), .in7(r7_q),
    .out(multiplexer_2_out), .sel(rt));
  and and_3 (hit1, and_1_out, eq1);
  and and_4 (hit2, and_2_out, eq2);
  Multiplexer #(.width(16)) multiplexer_3 (.in0(multiplexer_1_out), .in1(wd), .out(rd1), .sel(hit1));
  Multiplexer #(.width(16)) multiplexer_4 (.in0(multiplexer_2_out), .in1(wd), .out(rd2), .sel(hit2));
endmodule

module ControlUnit (
  input  [3:0] Opcode,
  output RegWrite,
  output MemRead,
  output MemWrite,
  output MemToReg,
  output RegDst,
  output ALUSrc,
  output BranchEq,
  output BranchNe,
  output Jump,
  output Jal,
  output Jr,
  output [2:0] ALUCtrl
);

  wire decoder_1_out2, decoder_1_out3, decoder_1_out4, decoder_1_out5, decoder_1_out6, decoder_1_out7,
       decoder_1_out8, decoder_1_out9, decoder_1_out12;

  Decoder #(.enable("false"), .select(4)) decoder_1 (
    .out0(MemRead), .out1(MemWrite), .out2(decoder_1_out2), .out3(decoder_1_out3), .out4(decoder_1_out4),
    .out5(decoder_1_out5), .out6(decoder_1_out6), .out7(decoder_1_out7), .out8(decoder_1_out8),
    .out9(decoder_1_out9), .out10(BranchEq), .out11(BranchNe), .out12(decoder_1_out12), .out13(Jal),
    .out14(Jr), .sel(Opcode));  // open: out15
  ROM #(.addrWidth(4), .dataWidth(3)) rom_1 (.addr(Opcode), .data(ALUCtrl));
  or or_1 (RegWrite, MemRead, decoder_1_out2, decoder_1_out3, decoder_1_out4, decoder_1_out5, decoder_1_out6, decoder_1_out7, decoder_1_out8, decoder_1_out9, Jal);
  or or_2 (RegDst, decoder_1_out2, decoder_1_out3, decoder_1_out4, decoder_1_out5, decoder_1_out6, decoder_1_out7, decoder_1_out8);
  or or_3 (ALUSrc, MemRead, MemWrite, decoder_1_out9);
  or or_4 (Jump, decoder_1_out12, Jal);

  assign MemToReg = MemRead;

  // Notes on the sheet:
  //   contents of rom_1 (hex, n*v repeats v):
  //   0 0 0 1 2 3 4 5 6 0 1 1
endmodule

module HazardUnit (
  input  [2:0] IDEX_rt,
  input  [2:0] IFID_rs,
  input  [2:0] IFID_rt,
  input  IDEX_MemRead,
  input  Jump,
  input  Jal,
  input  Jr,
  input  BranchTaken,
  output PCWrite,
  output IFID_Write,
  output IFID_Flush,
  output IDEX_Flush
);

  wire and_1_out, comparator_1_eq, comparator_2_eq, or_1_out, or_2_out;

  Comparator #(.width(3)) comparator_1 (.a(IDEX_rt), .b(IFID_rs), .eq(comparator_1_eq));  // open: gt, lt
  Comparator #(.width(3)) comparator_2 (.a(IDEX_rt), .b(IFID_rt), .eq(comparator_2_eq));  // open: gt, lt
  or or_1 (or_1_out, Jump, Jal, Jr);
  or or_2 (or_2_out, comparator_1_eq, comparator_2_eq);
  or or_3 (IFID_Flush, or_1_out, BranchTaken);
  and and_1 (and_1_out, IDEX_MemRead, or_2_out);
  not not_1 (IFID_Write, and_1_out);
  or or_4 (IDEX_Flush, and_1_out, IFID_Flush);

  assign PCWrite = IFID_Write;

  // Notes on the sheet:
  //   eq_rs
  //   eq_rt
  //   jump_flush
  //   rt_match
  //   CONTROL_FLUSH
  //   STALL
endmodule

module ID_EX (
  input  clk,
  input  reset,
  input  [15:0] pc1_in,
  input  [15:0] rd1_in,
  input  [15:0] rd2_in,
  input  [15:0] imm_in,
  input  [2:0] rs_in,
  input  [2:0] rt_in,
  input  [2:0] rd_in,
  input  [2:0] shamt_in,
  input  RegWrite_in,
  input  MemRead_in,
  input  MemWrite_in,
  input  MemToReg_in,
  input  RegDst_in,
  input  ALUSrc_in,
  input  BranchEq_in,
  input  BranchNe_in,
  input  [2:0] ALUCtrl_in,
  input  IDEX_Flush,
  output [15:0] pc1_out,
  output [15:0] rd1_out,
  output [15:0] rd2_out,
  output [15:0] imm_out,
  output [2:0] rs_out,
  output [2:0] rt_out,
  output [2:0] rd_out,
  output [2:0] shamt_out,
  output RegWrite_out,
  output MemRead_out,
  output MemWrite_out,
  output MemToReg_out,
  output RegDst_out,
  output ALUSrc_out,
  output BranchEq_out,
  output BranchNe_outv,
  output [2:0] ALUCtrl_out
);

  wire multiplexer_1_out, multiplexer_2_out, multiplexer_3_out, multiplexer_4_out, multiplexer_5_out,
       multiplexer_6_out, multiplexer_7_out, multiplexer_8_out;
  wire [2:0] multiplexer_9_out;

  Multiplexer multiplexer_1 (.in0(RegWrite_in), .in1(1'b0), .out(multiplexer_1_out), .sel(IDEX_Flush));
  Multiplexer multiplexer_2 (.in0(MemRead_in), .in1(1'b0), .out(multiplexer_2_out), .sel(IDEX_Flush));
  Multiplexer multiplexer_3 (.in0(MemWrite_in), .in1(1'b0), .out(multiplexer_3_out), .sel(IDEX_Flush));
  Multiplexer multiplexer_4 (.in0(MemToReg_in), .in1(1'b0), .out(multiplexer_4_out), .sel(IDEX_Flush));
  Multiplexer multiplexer_5 (.in0(RegDst_in), .in1(1'b0), .out(multiplexer_5_out), .sel(IDEX_Flush));
  Multiplexer multiplexer_6 (.in0(ALUSrc_in), .in1(1'b0), .out(multiplexer_6_out), .sel(IDEX_Flush));
  Multiplexer multiplexer_7 (.in0(BranchEq_in), .in1(1'b0), .out(multiplexer_7_out), .sel(IDEX_Flush));
  Multiplexer multiplexer_8 (.in0(BranchNe_in), .in1(1'b0), .out(multiplexer_8_out), .sel(IDEX_Flush));
  Multiplexer #(.width(3)) multiplexer_9 (.in0(ALUCtrl_in), .in1(3'b000), .out(multiplexer_9_out), .sel(IDEX_Flush));
  Register #(.width(16)) register_1 (.D(pc1_in), .en(1'b1), .clk(clk), .Q(pc1_out), .clr(reset));
  Register #(.width(16)) register_2 (.D(rd1_in), .en(1'b1), .clk(clk), .Q(rd1_out), .clr(reset));
  Register #(.width(16)) register_3 (.D(rd2_in), .en(1'b1), .clk(clk), .Q(rd2_out), .clr(reset));
  Register #(.width(16)) register_4 (.D(imm_in), .en(1'b1), .clk(clk), .Q(imm_out), .clr(reset));
  Register #(.width(3)) register_5 (.D(rs_in), .en(1'b1), .clk(clk), .Q(rs_out), .clr(reset));
  Register #(.width(3)) register_6 (.D(rt_in), .en(1'b1), .clk(clk), .Q(rt_out), .clr(reset));
  Register #(.width(3)) register_7 (.D(rd_in), .en(1'b1), .clk(clk), .Q(rd_out), .clr(reset));
  Register #(.width(3)) register_8 (.D(shamt_in), .en(1'b1), .clk(clk), .Q(shamt_out), .clr(reset));
  Register #(.width(1)) register_9 (.D(multiplexer_1_out), .en(1'b1), .clk(clk), .Q(RegWrite_out), .clr(reset));
  Register #(.width(1)) register_10 (.D(multiplexer_2_out), .en(1'b1), .clk(clk), .Q(MemRead_out), .clr(reset));
  Register #(.width(1)) register_11 (.D(multiplexer_3_out), .en(1'b1), .clk(clk), .Q(MemWrite_out), .clr(reset));
  Register #(.width(1)) register_12 (.D(multiplexer_4_out), .en(1'b1), .clk(clk), .Q(MemToReg_out), .clr(reset));
  Register #(.width(1)) register_13 (.D(multiplexer_5_out), .en(1'b1), .clk(clk), .Q(RegDst_out), .clr(reset));
  Register #(.width(1)) register_14 (.D(multiplexer_6_out), .en(1'b1), .clk(clk), .Q(ALUSrc_out), .clr(reset));
  Register #(.width(1)) register_15 (.D(multiplexer_7_out), .en(1'b1), .clk(clk), .Q(BranchEq_out), .clr(reset));
  Register #(.width(1)) register_16 (.D(multiplexer_8_out), .en(1'b1), .clk(clk), .Q(BranchNe_outv), .clr(reset));
  Register #(.width(3)) register_17 (.D(multiplexer_9_out), .en(1'b1), .clk(clk), .Q(ALUCtrl_out), .clr(reset));
endmodule

module EX_Stage (
  input  [15:0] rd2,
  input  ALUSrc,
  input  [15:0] imm,
  input  [2:0] ALUCtrl,
  input  [15:0] rd1,
  input  [2:0] shamt,
  input  [15:0] EXMEM_ALUResult,
  input  [2:0] rt,
  input  [15:0] MEMWB_WriteData,
  input  [2:0] rd,
  input  RegDst,
  input  [15:0] pc1,
  input  [1:0] ForwardA,
  input  BranchEq,
  input  BranchNe,
  input  [1:0] ForwardB,
  output [15:0] ALUResult,
  output Zero,
  output [2:0] WriteReg,
  output [15:0] BranchTarget,
  output [15:0] B_fwd,
  output BranchTaken
);

  wire and_1_out, and_2_out, not_1_out;
  wire [15:0] multiplexer_1_out, multiplexer_3_out;

  Multiplexer #(.select(2), .width(16)) multiplexer_1 (
    .in0(rd1), .in1(MEMWB_WriteData), .in2(EXMEM_ALUResult), .in3({16{1'b0}}), .out(multiplexer_1_out),
    .sel(ForwardA));
  Multiplexer #(.select(2), .width(16)) multiplexer_2 (
    .in0(rd2), .in1(MEMWB_WriteData), .in2(EXMEM_ALUResult), .in3({16{1'b0}}), .out(B_fwd), .sel(ForwardB));
  Multiplexer #(.width(16)) multiplexer_3 (.in0(B_fwd), .in1(imm), .out(multiplexer_3_out), .sel(ALUSrc));
  Multiplexer #(.width(3)) multiplexer_4 (.in0(rt), .in1(rd), .out(WriteReg), .sel(RegDst));
  Adder #(.width(16)) adder_1 (.a(pc1), .b(imm), .out(BranchTarget));  // open: cin, cout
  not not_1 (not_1_out, Zero);
  and and_1 (and_1_out, BranchEq, Zero);
  and and_2 (and_2_out, BranchNe, not_1_out);
  ALU alu_1 (
    .A(multiplexer_1_out), .B(multiplexer_3_out), .ALUCtrl(ALUCtrl), .shamt(shamt), .Result(ALUResult),
    .Zero(Zero));
  or or_1 (BranchTaken, and_1_out, and_2_out);

  // Notes on the sheet:
  //   ALU_A_raw = rd1
  //   A_fwd
  //   B_fwd
  //   ALU_B_raw
  //   beq_taken
  //   bne_taken
endmodule

module ALU (
  input  [15:0] A,
  input  [15:0] B,
  input  [2:0] ALUCtrl,
  input  [2:0] shamt,
  output [15:0] Result,
  output Zero
);

  wire comparator_1_lt;
  wire [3:0] bit_extender_1_out;
  wire [15:0] adder_1_out, adder_2_out, and_1_out, bit_extender_2_out, not_1_out, or_1_out, shifter_1_out,
       shifter_2_out;

  assign not_1_out = ~B;  // NOT_Gate not_1, 16 bits wide
  assign bit_extender_1_out = {{1{shamt[2]}}, shamt};  // Bit_Extender bit_extender_1
  Adder #(.width(16)) adder_1 (.a(A), .b(B), .out(adder_1_out));  // open: cin, cout
  Adder #(.width(16)) adder_2 (.a(A), .b(not_1_out), .out(adder_2_out), .cin(1'b1));  // open: cout
  assign and_1_out = A & B;  // AND_Gate and_1, 16 bits wide
  assign or_1_out = A | B;  // OR_Gate or_1, 16 bits wide
  Comparator #(.width(16)) comparator_1 (.a(A), .b(B), .lt(comparator_1_lt));  // open: gt, eq
  Shifter #(.width(16)) shifter_1 (.in(B), .\dist (bit_extender_1_out), .out(shifter_1_out));
  Shifter #(.shift("lr"), .width(16)) shifter_2 (.in(B), .\dist (bit_extender_1_out), .out(shifter_2_out));
  assign bit_extender_2_out = {{15{1'b0}}, comparator_1_lt};  // Bit_Extender bit_extender_2
  Multiplexer #(.select(3), .width(16)) multiplexer_1 (
    .in0(adder_1_out), .in1(adder_2_out), .in2(and_1_out), .in3(or_1_out), .in4(bit_extender_2_out),
    .in5(shifter_1_out), .in6(shifter_2_out), .in7({16{1'b0}}), .out(Result), .sel(ALUCtrl));
  Comparator #(.width(16)) comparator_2 (.a(Result), .b({16{1'b0}}), .eq(Zero));  // open: gt, lt

  // Notes on the sheet:
  //   add_res
  //   sub_res
  //   and_res
  //   or_res
  //   slt_bit
  //   sll_res
  //   srl_res
  //   slt_res
endmodule

module EX_MEM (
  input  clk,
  input  reset,
  input  [15:0] ALUResult_in,
  input  [15:0] rd2_in,
  input  [2:0] WriteReg_in,
  input  [15:0] BranchTarget_in,
  input  BranchTaken_in,
  input  MemRead_in,
  input  MemWrite_in,
  input  MemToReg_in,
  input  RegWrite_in,
  input  [2:0] Rt_in,
  output [15:0] ALUResult_out,
  output [15:0] rd2_out,
  output [2:0] WriteReg_out,
  output [15:0] BranchTarget_out,
  output BranchTaken_out,
  output MemRead_out,
  output MemWrite_out,
  output MemToReg_out,
  output RegWrite_out,
  output [2:0] Rt_out
);

  Register #(.width(16)) register_1 (.D(ALUResult_in), .en(1'b1), .clk(clk), .Q(ALUResult_out), .clr(reset));
  Register #(.width(16)) register_2 (.D(rd2_in), .en(1'b1), .clk(clk), .Q(rd2_out), .clr(reset));
  Register #(.width(3)) register_3 (.D(WriteReg_in), .en(1'b1), .clk(clk), .Q(WriteReg_out), .clr(reset));
  Register #(.width(16)) register_4 (.D(BranchTarget_in), .en(1'b1), .clk(clk), .Q(BranchTarget_out), .clr(reset));
  Register #(.width(1)) register_5 (.D(BranchTaken_in), .en(1'b1), .clk(clk), .Q(BranchTaken_out), .clr(reset));
  Register #(.width(1)) register_6 (.D(MemRead_in), .en(1'b1), .clk(clk), .Q(MemRead_out), .clr(reset));
  Register #(.width(1)) register_7 (.D(MemWrite_in), .en(1'b1), .clk(clk), .Q(MemWrite_out), .clr(reset));
  Register #(.width(1)) register_8 (.D(MemToReg_in), .en(1'b1), .clk(clk), .Q(MemToReg_out), .clr(reset));
  Register #(.width(1)) register_9 (.D(RegWrite_in), .en(1'b1), .clk(clk), .Q(RegWrite_out), .clr(reset));
  Register #(.width(3)) register_10 (.D(Rt_in), .en(1'b1), .clk(clk), .Q(Rt_out), .clr(reset));
endmodule

module DataMemory (
  input  clk,
  input  MemWrite,
  input  MemRead,
  input  [15:0] Addr,
  input  [15:0] WriteData,
  output [15:0] ReadData
);

  RAM #(.asyncread("true"), .dataWidth(16)) ram_1 (
    .addr(Addr[8:1]), .we(MemWrite), .oe(MemRead), .clk(clk), .din(WriteData), .dout(ReadData));
endmodule

module MEM_WB (
  input  clk,
  input  reset,
  input  [15:0] ReadData_in,
  input  [15:0] ALUResult_in,
  input  [2:0] WriteReg_in,
  input  [15:0] PC1_in,
  input  RegWrite_in,
  input  MemToReg_in,
  input  Jal_in,
  output [15:0] ReadData_out,
  output [15:0] ALUResult_out,
  output [2:0] WriteReg_out,
  output [15:0] PC1_out,
  output RegWrite_out,
  output MemToReg_out,
  output Jal_out
);

  Register #(.width(16)) register_1 (.D(ReadData_in), .en(1'b1), .clk(clk), .Q(ReadData_out), .clr(reset));
  Register #(.width(16)) register_2 (.D(ALUResult_in), .en(1'b1), .clk(clk), .Q(ALUResult_out), .clr(reset));
  Register #(.width(3)) register_3 (.D(WriteReg_in), .en(1'b1), .clk(clk), .Q(WriteReg_out), .clr(reset));
  Register #(.width(16)) register_4 (.D(PC1_in), .en(1'b1), .clk(clk), .Q(PC1_out), .clr(reset));
  Register #(.width(1)) register_5 (.D(RegWrite_in), .en(1'b1), .clk(clk), .Q(RegWrite_out), .clr(reset));
  Register #(.width(1)) register_6 (.D(MemToReg_in), .en(1'b1), .clk(clk), .Q(MemToReg_out), .clr(reset));
  Register #(.width(1)) register_7 (.D(Jal_in), .en(1'b1), .clk(clk), .Q(Jal_out), .clr(reset));
endmodule

module WBStage (
  input  RegWrite_in,
  input  [15:0] ReadData,
  input  [15:0] ALUResult,
  input  [15:0] PC1,
  input  MemToReg,
  input  Jal,
  input  [2:0] WriteReg_in,
  output RegWrite_out,
  output [15:0] WriteData_out,
  output [2:0] WriteReg_out
);

  wire [15:0] multiplexer_1_out;

  Multiplexer #(.width(16)) multiplexer_1 (.in0(ALUResult), .in1(ReadData), .out(multiplexer_1_out), .sel(MemToReg));
  Multiplexer #(.width(3)) multiplexer_2 (.in0(WriteReg_in), .in1(3'b111), .out(WriteReg_out), .sel(Jal));
  Multiplexer #(.width(16)) multiplexer_3 (.in0(multiplexer_1_out), .in1(PC1), .out(WriteData_out), .sel(Jal));
  or or_1 (RegWrite_out, RegWrite_in, Jal);

  // Notes on the sheet:
  //   wb data
endmodule

module ForwardingUnit (
  input  [2:0] EXMEM_Rd,
  input  [2:0] MEMWB_Rd,
  input  [2:0] IDEX_rs,
  input  EXMEM_RegWrite,
  input  MEMWB_RegWrite,
  input  [2:0] IDEX_rt,
  output [1:0] ForwardA,
  output [1:0] ForwardB
);

  wire and_1_out, and_3_out, and_5_out, comparator_1_eq, comparator_2_eq, comparator_3_eq, comparator_4_eq,
       comparator_5_eq, comparator_6_eq, not_1_out, not_2_out, not_3_out, not_4_out;

  Comparator #(.width(3)) comparator_1 (.a(MEMWB_Rd), .b(IDEX_rs), .eq(comparator_1_eq));  // open: gt, lt
  Comparator #(.width(3)) comparator_2 (.a(EXMEM_Rd), .b(3'b000), .eq(comparator_2_eq));  // open: gt, lt
  Comparator #(.width(3)) comparator_3 (.a(MEMWB_Rd), .b(3'b000), .eq(comparator_3_eq));  // open: gt, lt
  not not_1 (not_1_out, comparator_2_eq);
  not not_2 (not_2_out, comparator_3_eq);
  Comparator #(.width(3)) comparator_4 (.a(IDEX_rs), .b(EXMEM_Rd), .eq(comparator_4_eq));  // open: gt, lt
  Comparator #(.width(3)) comparator_5 (.a(EXMEM_Rd), .b(IDEX_rt), .eq(comparator_5_eq));  // open: gt, lt
  Comparator #(.width(3)) comparator_6 (.a(MEMWB_Rd), .b(IDEX_rt), .eq(comparator_6_eq));  // open: gt, lt
  and and_1 (and_1_out, EXMEM_RegWrite, not_1_out);
  and and_2 (ForwardA[1], and_1_out, comparator_4_eq);
  and and_3 (and_3_out, MEMWB_RegWrite, not_2_out, comparator_1_eq);
  not not_3 (not_3_out, ForwardA[1]);
  and and_4 (ForwardB[1], EXMEM_RegWrite, not_1_out, comparator_5_eq);
  and and_5 (and_5_out, MEMWB_RegWrite, not_2_out, comparator_6_eq);
  and and_6 (ForwardA[0], not_3_out, and_3_out);
  not not_4 (not_4_out, ForwardB[1]);
  and and_7 (ForwardB[0], not_4_out, and_5_out);

  // Notes on the sheet:
  //   eq_memwb_rs
  //   eq0_exmem
  //   eq0_memwb
  //   exmem_not0
  //   memwb_not0
  //   eq_exmem_rs
  //   eq_exmem_rt
  //   eq_memwb_rt
  //   tmp_ex1
  //   exmem_match_rs
  //   memwb_match_rs
  //   exmem_match_rt
  //   memwb_match_rt
  //   not_exmem_rs
endmodule

module CycleCounter (
  input  clk,
  input  reset,
  output [15:0] count
);

  Counter #(.max('hffff), .width(16)) counter_1 (
    .count(1'b1), .Q(count), .clk(clk), .clr(reset));  // open: load, D, carry, up
endmodule
